# Fritzing sketch Esp8266Veri+LCD (saved by Fritzing 0.9.3b)
breadboards: 1

parts:
  U1 = ESP8266 WiFi Module [part_number=ESP8266]
  LCD1 = LCD screen
  U2 = POT [package=alps_pot]
  Parça1 = Arduino Uno (Rev3)

nets:
  N1: U1.RXD, Parça1.D9_PWM
  VCC: U1.VCC, U1.CH_PD, Parça1.3V3
  GND: U1.GND, LCD1.VSS, LCD1.R/W, U2.A, Parça1.GND
  N2: U1.TXD, Parça1.D8
  VDD: LCD1.VDD, LCD1.LED-, U2.E, Parça1.5V
  N3: LCD1.V0, U2.S
  N4: LCD1.RS, Parça1.D12/MISO
  N5: LCD1.E, Parça1.D11_PWM/MOSI
  N6: LCD1.DB4, Parça1.D5_PWM
  N7: LCD1.DB5, Parça1.D4
  N8: LCD1.DB6, Parça1.D3_PWM
  N9: LCD1.DB7, Parça1.D2
  N10: LCD1.LED+, Parça1.D1/TX

custom parts:
  ESP8266 WiFi Module: Generic WiFi Module based on the ESP8266 with onboard PCB antenna and UART communications
